// Logisim project cpu.circ as structural Verilog: 1 circuit, main circuit main
module main (
);

  wire clock, counter_1_q, counter_2_q, counter_3_q, FDX_state_0, FDX_state_1, not_1_out, not_2_out,
       not_3_out, str_RAM;
  wire [7:0] PC;
  wire [15:0] RAM;

  Clock clock_1 (.out(clock));
  not not_1 (not_1_out, clock);
  Register AC ();  // open: D, en, Q, clk, clr
  Register #(.width(16)) IR (.D(RAM), .clk(FDX_state_0));  // open: en, Q, clr
  not not_2 (not_2_out, counter_1_q);
  Counter #(.width(1), .max('h1)) counter_1 (.Q(counter_1_q), .clk(clock));  // open: load, D, count, carry, clr
  Counter #(.width(1), .max('h1)) counter_2 (.Q(counter_2_q), .clk(not_1_out));  // open: load, D, count, carry, clr
  not not_3 (not_3_out, counter_2_q);
  and and_1 (FDX_state_0, not_2_out, clock);
  and and_2 (FDX_state_1, counter_1_q, not_3_out);
  Counter #(.width(1), .max('h1)) counter_3 (.Q(counter_3_q), .clk(clock));  // open: load, D, count, carry, clr
  Counter #(.width(1), .max('h1)) counter_4 (.clk(FDX_state_1));  // open: load, D, count, Q, carry, clr
  Counter u_PC (.Q(PC), .clk(FDX_state_1));  // open: load, D, count, carry, clr
  // ula ula_1: pin names not known
  RAM #(.dataWidth(16), .bus("separate")) ram_1 (.addr(PC), .data(RAM), .str(str_RAM));  // open: din, sel, clk, ld, clr

  // Notes on the sheet:
  //   <------------
  //   conectando o clock diretamente
  //   chegávamos a problemas de delay
endmodule
